# Fritzing sketch schematisation cablage (saved by Fritzing 0.9.6b)
breadboards: 1

parts:
  IC1 = MQ-2 [package="DIP (Dual Inline) [THT]"]
  J1 = Piezo Speaker
  Composant2 = Arduino Uno (Rev3)
  R2 = Resistor [tolerance=±5% power=0.25 resistance=220 package=THT]
  JACK1 = 2.1mm Barrel Jack with Terminal Block
  GSM_SIM_GPSR_SMS_SIM900_SIM1 = SIM800L [package=THT]
  DC1 = DC_DC_XL4016 [package=board_screw]
  R3 = Resistor [tolerance=±5% power=0.25 resistance=220 package=THT]  # not connected
  LED2 = smd LED [color="Red (660nm)" package="0805 [SMD]"]
  LED1 = smd LED [color="Green (560nm)" package="0603 [SMD]"]  # not connected

nets:
  N1: IC1.pin1, Composant2.5V
  N2: IC1.pin2, J1.pin1, Composant2.GND, JACK1.NEG, GSM_SIM_GPSR_SMS_SIM900_SIM1.GND#5, DC1.IN-
  N3: IC1.pin3, Composant2.A0
  N4: J1.pin2, Composant2.D9_PWM
  N5: Composant2.D8, R2.Pin_0
  N6: Composant2.D10_PWM/SS, GSM_SIM_GPSR_SMS_SIM900_SIM1.SIM_TXD
  N7: Composant2.D11_PWM/MOSI, GSM_SIM_GPSR_SMS_SIM900_SIM1.SIM_RXD
  N8: Composant2.VIN, JACK1.POS, DC1.IN+
  N9: R2.Pin_1, LED2.cathode
  N10: GSM_SIM_GPSR_SMS_SIM900_SIM1.5V, DC1.OUT+
  N11: GSM_SIM_GPSR_SMS_SIM900_SIM1.GND#1, DC1.OUT-

custom parts:
  MQ-2: MQ-2 Gas Sensor module
